# Fritzing sketch proyecto5-esquema (saved by Fritzing 0.9.3b)
circuit board: 6.88566cm x 5.36311cm
breadboards: 1

parts:
  LED1 = LED - 5mm [color="Red (633nm)" package="5 mm [THT]"]
  LED2 = LED - 5mm [color="Yellow (592nm)" package="5 mm [THT]"]
  LED3 = LED - 5mm [color="Green (555nm)" package="5 mm [THT]"]
  LED4 = LED - 5mm [color="Red (633nm)" package="5 mm [THT]"]
  LED5 = LED - 5mm [color="Green (555nm)" package="5 mm [THT]"]
  R6 = Resistor [tolerance=±5% resistance=100k package=THT]
  Arduino1 = Arduino Uno (Rev3)
  S2 = Pushbutton [package="[THT]"]

nets:
  N1: LED1.cathode, LED2.cathode, LED3.cathode, LED4.cathode, LED5.cathode, R6.Pin_1, Arduino1.GND
  N2: LED1.anode, Arduino1.D12/MISO
  N3: LED2.anode, Arduino1.D11_PWM/MOSI
  N4: LED3.anode, Arduino1.D10_PWM/SS
  N5: LED4.anode, Arduino1.D9_PWM
  N6: LED5.anode, Arduino1.D8
  N7: R6.Pin_0, Arduino1.D2, S2.Pin_1, S2.Pin_2
  N8: Arduino1.5V, S2.Pin_3, S2.Pin_4

notes:
  Semáforo para peatones
  Semáforo para coches
