# Fritzing sketch proyecto2-esquema (saved by Fritzing 0.9.3b)

parts:
  Arduino1 = Arduino Uno (Rev3)
  LED1 = LED - 5mm [color="Red (633nm)" package="5 mm [THT]"]

nets:
  N1: Arduino1.D13/SCK, LED1.anode
  N2: Arduino1.GND, LED1.cathode
