# Fritzing sketch proyecto4-esquema (saved by Fritzing 0.9.3b)
circuit board: 6.88566cm x 5.36311cm
breadboards: 1

parts:
  LED1 = LED - 5mm [color="Red (633nm)" package="5 mm [THT]"]
  LED2 = LED - 5mm [color="Yellow (592nm)" package="5 mm [THT]"]
  LED3 = LED - 5mm [color="Green (555nm)" package="5 mm [THT]"]
  Arduino1 = Arduino Uno (Rev3)

nets:
  N1: LED1.cathode, LED2.cathode, LED3.cathode, Arduino1.GND
  N2: LED1.anode, Arduino1.D12/MISO
  N3: LED2.anode, Arduino1.D11_PWM/MOSI
  N4: LED3.anode, Arduino1.D10_PWM/SS

notes:
  Semáforo para coches
